// Logisim project CW1.circ as structural Verilog: 2 circuits, main circuit main
module main (
  output out_1
);

  wire and_2_out, and_4_out, and_5_out, and_6_out, button_1_out, cdm_8_1_data_code_prime, cdm_8_1_mem, clk,
       clock_1_out, controlled_buffer_1_out, Data, decoder_1_out0, decoder_1_out1, decoder_1_out2, DMEM,
       Inst, IOSel, nand_1_out, not_1_out, not_2_out, or_1_out, or_2_out, RAMen, RAMout, rd_wr_prime,
       undriven;
  wire [2:0] IOAddr;
  wire [7:0] cdm_8_1_data_out, cdm_8_1_pc, cdm_8_1_ps, cdm_8_1_r0, cdm_8_1_r1, cdm_8_1_r2, cdm_8_1_r3,
       cdm_8_1_sp, cheaporam_1_d_out, controlled_buffer_3_out, IOData, RAMin, register_1_q, register_2_q;
  wire [7:3] cdm_8_1_addr;

  // Probe on cdm_8_1_r0
  or or_1 (or_1_out, RAMen, clock_1_out);
  Clock clock_1 (.out(clock_1_out));
  Decoder #(.select(3), .disabled(0)) decoder_1 (
    .out0(decoder_1_out0), .out1(decoder_1_out1), .out2(decoder_1_out2), .sel(IOAddr), .en(IOSel));  // open: out3, out4, out5, out6, out7
  // Probe on cdm_8_1_r2
  // Probe on cdm_8_1_pc
  // Probe on cdm_8_1_r3
  // Probe on cdm_8_1_r1
  Button button_1 (.out(button_1_out));
  and and_1 (clk, ~RAMen, clock_1_out);  // AND_Gate
  and and_2 (and_2_out, rd_wr_prime, undriven);
  // Probe on cdm_8_1_sp
  // Probe on cdm_8_1_ps
  not not_1 (not_1_out, nand_1_out);
  and and_3 (IOSel, not_1_out, clk, Data);
  and and_4 (and_4_out, decoder_1_out0, ~rd_wr_prime);  // AND_Gate
  and and_5 (and_5_out, decoder_1_out1, ~rd_wr_prime);  // AND_Gate
  and and_6 (and_6_out, decoder_1_out2, ~rd_wr_prime);  // AND_Gate
  and and_7 (RAMout, decoder_1_out2, rd_wr_prime);
  assign controlled_buffer_1_out = and_2_out ? out_1 : 1'bz;  // Controlled_Buffer controlled_buffer_1
  Decoder #(.disabled(0)) decoder_2 (.out0(Inst), .out1(Data), .sel(cdm_8_1_data_code_prime), .en(cdm_8_1_mem));
  CdM_8 cdm_8_1 (
    .data_code_prime(cdm_8_1_data_code_prime), .R0(cdm_8_1_r0), .R1(cdm_8_1_r1), .mem(cdm_8_1_mem),
    .R2(cdm_8_1_r2), .load_st_prime(rd_wr_prime), .R3(cdm_8_1_r3), .addr({cdm_8_1_addr, IOAddr}),
    .PC(cdm_8_1_pc), .SP(cdm_8_1_sp), .data_out(cdm_8_1_data_out), .data_in(controlled_buffer_3_out),
    .PS(cdm_8_1_ps), .clk(or_1_out), .rset(button_1_out));  // open: page, IAck, IRQ, vector, shadow
  and and_8 (DMEM, nand_1_out, Data);
  Register #(.trigger("high")) register_1 (.D(IOData), .en(and_4_out), .Q(register_1_q), .clk(and_4_out));  // open: clr
  Register #(.trigger("high")) register_2 (.D(IOData), .en(and_5_out), .Q(register_2_q), .clk(and_5_out));  // open: clr
  Register #(.trigger("high")) register_3 (.D(IOData), .en(and_6_out), .Q(RAMin), .clk(and_6_out));  // open: clr
  D_Flip_Flop d_ff_1 (
    .clk(decoder_1_out2), .D(decoder_1_out2), .Q(RAMen), .en(decoder_1_out2), .reset(out_1));  // open: Qn, preset
  assign IOData = not_2_out ? cdm_8_1_data_out : 8'bz;  // Controlled_Buffer controlled_buffer_2
  not not_2 (not_2_out, rd_wr_prime);
  assign controlled_buffer_3_out = rd_wr_prime ? IOData : 8'bz;  // Controlled_Buffer controlled_buffer_3
  nand nand_1 (nand_1_out, cdm_8_1_addr[3], cdm_8_1_addr[4], cdm_8_1_addr[5], cdm_8_1_addr[6], cdm_8_1_addr[7]);
  or or_2 (or_2_out, RAMen, rd_wr_prime);
  CheapoRAM cheaporam_1 (
    .Adr({register_1_q, register_2_q}), .En(or_2_out), .Rd_Wr_prime(rd_wr_prime), .D_Out(cheaporam_1_d_out),
    .D_In(RAMin), .Rdy(out_1));
  ROM rom_1 (.addr({cdm_8_1_addr, IOAddr}), .data(IOData), .sel(Inst));
  // Probe on IOData
  RAM ram_1 (.addr({cdm_8_1_addr, IOAddr}), .data(IOData), .sel(DMEM), .clk(clk), .ld(rd_wr_prime));  // open: clr
  assign IOData = RAMout ? cheaporam_1_d_out : 8'bz;  // Controlled_Buffer controlled_buffer_4

  // Other names for the same wires on the sheet: RAMclr = out_1

  // Notes on the sheet:
  //   High Order Addr
  //   Low Order Addr
  //   Data Write
  //   Enable RAM
  //   contents of rom_1 (hex, n*v repeats v):
  //   d0 f0 c8 d6 6 d4 d0 0 d1 10 d2 16 d6 22 d0 1 d1 0 d6 2e d0 1 d1 10 d2 31 d6 22 d0 1 d1 1 d6 2e c3 d3
  //   f8 ac d3 f9 ad d3 fa ae c7 d7 c3 d3 f8 ac d3 f9 ad d3 fa be c7 d7
endmodule

module Von_Neumann (
  output out_1
);

  wire button_1_out, clk, IOSel, mem, memSel, nand_1_out, not_1_out, not_2_out, rd_wr_prime;
  wire [7:0] addr, cdm_8_1_data_out, cdm_8_1_pc, cdm_8_1_ps, cdm_8_1_r0, cdm_8_1_r1, cdm_8_1_r2, cdm_8_1_r3,
       cdm_8_1_sp, cheaporam_1_d_out, controlled_buffer_1_out;
  wire [15:15] pull_resistor_1_node;

  // Probe on cdm_8_1_r1
  // Probe on cdm_8_1_r2
  // Probe on cdm_8_1_r0
  Button button_1 (.out(button_1_out));
  Clock clock_1 (.out(clk));
  and and_1 (IOSel, not_1_out, clk, mem);
  Pull_Resistor pull_resistor_1 (.node(pull_resistor_1_node[15]));
  // Probe on cdm_8_1_r3
  // Probe on cdm_8_1_sp
  // Probe on cdm_8_1_pc
  not not_1 (not_1_out, nand_1_out);
  and and_2 (memSel, nand_1_out, mem);
  // Probe on cdm_8_1_ps
  nand nand_1 (nand_1_out, addr[0], addr[1], addr[2], addr[3], addr[4], addr[5], addr[6], addr[7]);
  CdM_8 cdm_8_1 (
    .R0(cdm_8_1_r0), .R1(cdm_8_1_r1), .mem(mem), .R2(cdm_8_1_r2), .load_st_prime(rd_wr_prime),
    .R3(cdm_8_1_r3), .addr(addr), .PC(cdm_8_1_pc), .SP(cdm_8_1_sp), .data_out(cdm_8_1_data_out),
    .data_in(controlled_buffer_1_out), .PS(cdm_8_1_ps), .clk(clk), .rset(button_1_out));  // open: data_code_prime, page, IAck, IRQ, vector, shadow
  assign controlled_buffer_1_out = rd_wr_prime ? cheaporam_1_d_out : 8'bz;  // Controlled_Buffer controlled_buffer_1
  CheapoRAM cheaporam_1 (
    .Adr({{8{pull_resistor_1_node[15]}}, addr}), .En(IOSel), .Rd_Wr_prime(rd_wr_prime),
    .D_Out(cheaporam_1_d_out), .D_In(cheaporam_1_d_out), .Rdy(out_1));
  assign cheaporam_1_d_out = not_2_out ? cdm_8_1_data_out : 8'bz;  // Controlled_Buffer controlled_buffer_2
  not not_2 (not_2_out, rd_wr_prime);
  RAM ram_1 (.addr(addr), .data(cheaporam_1_d_out), .sel(memSel), .clk(clk), .ld(rd_wr_prime));  // open: clr
endmodule
