// Logisim project CW2.circ as structural Verilog: 2 circuits, main circuit main
module main (
);

  wire and_1_out, and_4_out, and_6_out, and_7_out, and_8_out, and_9_out, and_10_out, and_12_out, and_13_out,
       and_14_out, and_19_out, button_1_out, captureClr, captureEn, cdm_8_1_data_code_prime, cdm_8_1_mem,
       charReady, clk, clock_1_out, Data, decoder_1_out0, decoder_1_out1, decoder_1_out2, DMEM, EOS_out,
       Inst, IOSel, keyboard_1_avail, keyClr, nand_1_out, noCapture, noStringWrite, not_1_out, not_2_out,
       not_3_out, not_4_out, not_5_out, not_6_out, not_7_out, or_1_out, or_2_out, or_3_out, or_4_out,
       or_5_out, or_6_out, or_7_out, r_out, RAMclr, RAMenable, RAMout, rd_wr_prime, reading, readReady,
       s_out, stringEnd, stringWrite, TTY_Key, writeReady, xor_1_out;
  wire [6:0] ASCIIrd, controlled_buffer_1_out, ram_1_data;
  wire [7:0] addr, cdm_8_1_data_out, cdm_8_1_pc, cdm_8_1_ps, cdm_8_1_r0, cdm_8_1_r1, cdm_8_1_r2, cdm_8_1_r3,
       cdm_8_1_sp, cheaporam_1_d_out, controlled_buffer_4_out, counter_1_q, IOData, readFromRAM,
       register_1_q, register_2_q, register_3_q;
  wire [7:7] pull_resistor_3_node;

  not not_1 (not_1_out, rd_wr_prime);
  and and_1 (and_1_out, writeReady, charReady);
  and and_2 (readReady, not_1_out, TTY_Key);
  and and_3 (writeReady, TTY_Key, rd_wr_prime);
  or or_1 (or_1_out, writeReady, stringWrite);
  // Probe on cdm_8_1_r0
  or or_2 (or_2_out, RAMenable, clock_1_out);
  Clock clock_1 (.out(clock_1_out));
  Decoder #(.select(3), .disabled(0)) decoder_1 (
    .out0(decoder_1_out0), .out1(decoder_1_out1), .out2(decoder_1_out2), .out3(TTY_Key), .sel(addr[2:0]),
    .en(IOSel));  // open: out4, out5, out6, out7
  and and_4 (and_4_out, stringWrite, RAMclr);
  or or_3 (or_3_out, and_4_out, and_1_out);
  // Probe on cdm_8_1_r2
  // Probe on cdm_8_1_r3
  // Probe on cdm_8_1_pc
  // Probe on cdm_8_1_r1
  Button button_1 (.out(button_1_out));
  and and_5 (clk, ~RAMenable, clock_1_out);  // AND_Gate
  or or_4 (or_4_out, readReady, and_6_out);
  and and_6 (and_6_out, captureEn, writeReady);
  Counter counter_1 (.count(or_3_out), .Q(counter_1_q), .clk(or_3_out), .clr(or_5_out));  // open: load, D, carry
  or or_5 (or_5_out, stringEnd, and_7_out);
  and and_7 (and_7_out, stringWrite, not_2_out);
  not not_2 (not_2_out, stringWrite);
  // Probe on cdm_8_1_ps
  // Probe on cdm_8_1_sp
  and and_8 (and_8_out, decoder_1_out0, ~rd_wr_prime);  // AND_Gate
  and and_9 (and_9_out, decoder_1_out1, ~rd_wr_prime);  // AND_Gate
  and and_10 (and_10_out, decoder_1_out2, ~rd_wr_prime);  // AND_Gate
  and and_11 (RAMout, decoder_1_out2, rd_wr_prime);
  or or_6 (or_6_out, stringWrite, captureEn);
  Decoder #(.disabled(0)) decoder_2 (.out0(Inst), .out1(Data), .sel(cdm_8_1_data_code_prime), .en(cdm_8_1_mem));
  CdM_8 cdm_8_1 (
    .data_code_prime(cdm_8_1_data_code_prime), .R0(cdm_8_1_r0), .R1(cdm_8_1_r1), .mem(cdm_8_1_mem),
    .R2(cdm_8_1_r2), .load_st_prime(rd_wr_prime), .R3(cdm_8_1_r3), .addr(addr), .PC(cdm_8_1_pc),
    .SP(cdm_8_1_sp), .data_out(cdm_8_1_data_out), .data_in(controlled_buffer_4_out), .PS(cdm_8_1_ps),
    .clk(or_2_out), .rset(button_1_out));  // open: page, IAck, IRQ, vector, shadow
  Register #(.trigger("high")) register_1 (.D(IOData), .en(and_8_out), .Q(register_1_q), .clk(and_8_out));  // open: clr
  Register #(.trigger("high")) register_2 (.D(IOData), .en(and_9_out), .Q(register_2_q), .clk(and_9_out));  // open: clr
  Register #(.trigger("high")) register_3 (
    .D(IOData), .en(and_10_out), .Q(register_3_q), .clk(and_10_out));  // open: clr
  D_Flip_Flop d_ff_1 (
    .clk(decoder_1_out2), .D(decoder_1_out2), .Q(RAMenable), .en(decoder_1_out2), .reset(RAMclr));  // open: Qn, preset
  assign {captureClr, controlled_buffer_1_out} = readReady ? IOData : 8'bz;  // Controlled_Buffer controlled_buffer_1
  assign controlled_buffer_1_out = writeReady ? ASCIIrd : 7'bz;  // Controlled_Buffer controlled_buffer_2
  RAM #(.dataWidth(7), .bus("separate")) ram_1 (
    .addr(counter_1_q), .din(ASCIIrd), .data(ram_1_data), .str(and_1_out), .sel(or_6_out), .clk(and_1_out),
    .ld(or_1_out), .clr(stringEnd));
  assign IOData = not_3_out ? cdm_8_1_data_out : 8'bz;  // Controlled_Buffer controlled_buffer_3
  not not_3 (not_3_out, rd_wr_prime);
  assign controlled_buffer_4_out = rd_wr_prime ? IOData : 8'bz;  // Controlled_Buffer controlled_buffer_4
  TTY tty_1 (.data(controlled_buffer_1_out), .clk(or_4_out), .clr(captureClr));  // open: we
  Pull_Resistor pull_resistor_1 (.node(captureClr));
  Pull_Resistor #(.pull(1)) pull_resistor_2 (.node(ram_1_data));
  Keyboard #(.trigger("falling")) keyboard_1 (
    .clk(xor_1_out), .clr(captureClr), .avail(keyboard_1_avail), .data(ASCIIrd));  // open: re
  xor xor_1 (xor_1_out, writeReady, keyClr);
  and EOS (EOS_out, ~ram_1_data[0], ~ram_1_data[1], ~ram_1_data[2], ~ram_1_data[3], ~ram_1_data[4], ~ram_1_data[5], ~ram_1_data[6]);  // AND_Gate
  and and_12 (and_12_out, stringWrite, writeReady);
  or or_7 (or_7_out, RAMenable, rd_wr_prime);
  CheapoRAM cheaporam_1 (
    .Adr({register_1_q, register_2_q}), .En(or_7_out), .Rd_Wr_prime(rd_wr_prime), .D_Out(cheaporam_1_d_out),
    .D_In(register_3_q), .Rdy(RAMclr));
  and and_13 (and_13_out, TTY_Key, not_4_out);
  not not_4 (not_4_out, and_14_out);
  and and_14 (and_14_out, writeReady, not_5_out);
  not not_5 (not_5_out, reading);
  and and_15 (stringEnd, EOS_out, and_12_out);
  ROM rom_1 (.addr(addr), .data(IOData), .sel(Inst));
  // Probe on IOData
  RAM ram_2 (.addr(addr), .data(IOData), .sel(DMEM), .clk(clk), .ld(rd_wr_prime));  // open: clr
  assign IOData = RAMout ? cheaporam_1_d_out : 8'bz;  // Controlled_Buffer controlled_buffer_5
  // Probe on ASCIIrd
  and and_16 (charReady, keyboard_1_avail, captureEn);
  assign IOData = and_13_out ? readFromRAM : 8'bz;  // Controlled_Buffer controlled_buffer_6
  assign IOData = and_14_out ? {stringWrite, ram_1_data} : 8'bz;  // Controlled_Buffer controlled_buffer_7
  and and_17 (IOSel, not_6_out, clk, Data);
  // Probe on ASCIIrd
  not not_6 (not_6_out, nand_1_out);
  and and_18 (DMEM, nand_1_out, Data);
  and s (s_out, ASCIIrd[0], ASCIIrd[1], ~ASCIIrd[2], ~ASCIIrd[3], ASCIIrd[4], ASCIIrd[5], ASCIIrd[6]);  // AND_Gate
  and \return  (captureClr, ~ASCIIrd[0], ASCIIrd[1], ~ASCIIrd[2], ASCIIrd[3], ~ASCIIrd[4], ~ASCIIrd[5], ~ASCIIrd[6]);  // AND_Gate
  and r (r_out, ~ASCIIrd[0], ASCIIrd[1], ~ASCIIrd[2], ~ASCIIrd[3], ASCIIrd[4], ASCIIrd[5], ASCIIrd[6]);  // AND_Gate
  nand nand_1 (nand_1_out, addr[3], addr[4], addr[5], addr[6], addr[7]);
  Pull_Resistor #(.pull(1)) pull_resistor_3 (.node(pull_resistor_3_node[7]));
  D_Flip_Flop Capture_Start (
    .clk(s_out), .D(s_out), .Q(captureEn), .Qn(noCapture), .en(s_out), .reset(captureClr));  // open: preset
  D_Flip_Flop RAM_write_start (
    .clk(captureClr), .D(captureClr), .Q(stringWrite), .Qn(noStringWrite), .en(captureClr), .reset(stringEnd));  // open: preset
  and and_19 (and_19_out, r_out, noCapture, noStringWrite);
  not not_7 (not_7_out, captureEn);
  D_Flip_Flop d_ff_2 (
    .clk(and_19_out), .D(and_19_out), .Q(reading), .en(and_19_out), .reset(readReady));  // open: Qn, preset
  assign readFromRAM = reading ? {8{pull_resistor_3_node[7]}} : 8'bz;  // Controlled_Buffer controlled_buffer_8
  and and_20 (keyClr, not_7_out, captureEn);

  // Other names for the same wires on the sheet: IOAddr[2:0] = addr[2:0]

  // Notes on the sheet:
  //   Read signal
  //   Write Signal
  //   High Order Addr
  //   Low Order Addr
  //   Data Write
  //   Enable RAM
  //   Key Input Buffer
  //   contents of rom_1 (hex, n*v repeats v):
  //   d0 f0 c8 d6 3a d4 d0 0 d1 10 d2 16 d6 22 d0 1 d1 0 d6 2e d0 1 d1 10 d2 31 d6 22 d0 1 d1 1 d6 2e c3
  //   d3 f8 ac d3 f9 ad d3 fa ae c7 d7 c3 d3 f8 ac d3 f9 ad d3 fa be c7 d7 d6 5c d6 40 ee 3a d0 fb b1 25
  //   e2 4c d0 80 d1 0 a1 d7 5 91 6 d0 80 b1 30 d6 22 8d d0 80 a1 ee 40 d7 d0 fb b1 d2 ff 49 79 e1 7d d0
  //   80 b1 30 d6 2e a e0 78 d0 fb a2 d0 80 b1 8d a1 ee 65 d0 80 d1 0 a1 d7
  //   Memory Mapped I/O
  //   Command Key Capture
endmodule

module Von_Neumann (
  output out_1
);

  wire button_1_out, clk, IOSel, mem, memSel, nand_1_out, not_1_out, not_2_out, rd_wr_prime;
  wire [7:0] addr, cdm_8_1_data_out, cdm_8_1_pc, cdm_8_1_ps, cdm_8_1_r0, cdm_8_1_r1, cdm_8_1_r2, cdm_8_1_r3,
       cdm_8_1_sp, cheaporam_1_d_out, controlled_buffer_1_out;
  wire [15:15] pull_resistor_1_node;

  // Probe on cdm_8_1_r2
  // Probe on cdm_8_1_r0
  // Probe on cdm_8_1_r1
  Clock clock_1 (.out(clk));
  Button button_1 (.out(button_1_out));
  and and_1 (IOSel, not_1_out, clk, mem);
  Pull_Resistor pull_resistor_1 (.node(pull_resistor_1_node[15]));
  // Probe on cdm_8_1_sp
  // Probe on cdm_8_1_pc
  // Probe on cdm_8_1_r3
  not not_1 (not_1_out, nand_1_out);
  and and_2 (memSel, nand_1_out, mem);
  // Probe on cdm_8_1_ps
  nand nand_1 (nand_1_out, addr[0], addr[1], addr[2], addr[3], addr[4], addr[5], addr[6], addr[7]);
  CdM_8 cdm_8_1 (
    .R0(cdm_8_1_r0), .R1(cdm_8_1_r1), .mem(mem), .R2(cdm_8_1_r2), .load_st_prime(rd_wr_prime),
    .R3(cdm_8_1_r3), .addr(addr), .PC(cdm_8_1_pc), .SP(cdm_8_1_sp), .data_out(cdm_8_1_data_out),
    .data_in(controlled_buffer_1_out), .PS(cdm_8_1_ps), .clk(clk), .rset(button_1_out));  // open: data_code_prime, page, IAck, IRQ, vector, shadow
  assign controlled_buffer_1_out = rd_wr_prime ? cheaporam_1_d_out : 8'bz;  // Controlled_Buffer controlled_buffer_1
  CheapoRAM cheaporam_1 (
    .Adr({{8{pull_resistor_1_node[15]}}, addr}), .En(IOSel), .Rd_Wr_prime(rd_wr_prime),
    .D_Out(cheaporam_1_d_out), .D_In(cheaporam_1_d_out), .Rdy(out_1));
  assign cheaporam_1_d_out = not_2_out ? cdm_8_1_data_out : 8'bz;  // Controlled_Buffer controlled_buffer_2
  not not_2 (not_2_out, rd_wr_prime);
  RAM ram_1 (.addr(addr), .data(cheaporam_1_d_out), .sel(memSel), .clk(clk), .ld(rd_wr_prime));  // open: clr
endmodule
