// Logisim project CW3.circ as structural Verilog: 2 circuits, main circuit main
module main (
);

  wire and_1_out, and_5_out, and_6_out, and_7_out, and_8_out, and_10_out, and_11_out, and_12_out, and_14_out,
       and_15_out, and_17_out, and_18_out, and_21_out, and_23_out, and_24_out, and_25_out, and_29_out,
       and_30_out, and_31_out, bufferClr, button_1_out, captureEn, cdm_8_1_data_code_prime, cdm_8_1_mem, clk,
       clock_1_out, clock_2_out, clock_3_out, d_ff_2_q, d_ff_3_q, Data, decoder_1_out0, decoder_1_out1,
       decoder_1_out2, DMEM, EOS_2_out, EOS_out, filenameRd, filenameRdStart, filenameRdStop, filenameWrite,
       filenameWrStop, getFile, Inst, IOSel, keyboard_1_avail, keybrdClr, keyClr, keyReady, nand_1_out,
       noCapture, noFilename, nor_4_out, nor_5_out, noStringWrite, not_1_out, not_2_out, not_3_out,
       not_4_out, not_5_out, not_6_out, not_7_out, not_8_out, not_9_out, not_10_out, not_11_out, not_12_out,
       not_13_out, not_14_out, not_15_out, not_16_out, not_17_out, not_18_out, not_19_out, not_20_out,
       not_21_out, not_22_out, or_1_out, or_2_out, or_3_out, or_4_out, or_5_out, or_6_out, or_7_out,
       or_8_out, or_9_out, or_10_out, or_11_out, or_12_out, or_13_out, or_14_out, or_16_out, Prompt_OK_out,
       promptClk, r_out, RAMclr, RAMenable, RAMout, rd_wr_prime, readReady, restart, return_out, s_out,
       s_r_ff_1_q, stringEnd, stringRead, stringWrite, TTY_Key, TTYclr, writeReady, xor_1_out;
  wire [2:0] priority_encoder_1_out;
  wire [6:0] ASCIIrd, keyboard_1_data, multiplexer_1_out, promptData, writeToRAM;
  wire [7:0] addr, bit_extender_1_out, cdm_8_1_data_out, cdm_8_1_pc, cdm_8_1_ps, cdm_8_1_r0, cdm_8_1_r1,
       cdm_8_1_r2, cdm_8_1_r3, cdm_8_1_sp, cheaporam_1_d_out, controlled_buffer_2_out,
       controlled_buffer_3_out, counter_1_q, counter_2_q, IOData, multiplier_1_out, pull_resistor_4_node,
       readFromRAM, register_1_q, register_2_q, register_3_q;
  wire [7:7] and_13_out, and_16_out, pull_resistor_5_node;

  or or_1 (or_1_out, RAMenable, clock_1_out);
  Clock clock_1 (.out(clock_1_out));
  Decoder #(.select(3), .disabled(0)) decoder_1 (
    .out0(decoder_1_out0), .out1(decoder_1_out1), .out2(decoder_1_out2), .out3(TTY_Key), .sel(addr[2:0]),
    .en(IOSel));  // open: out4, out5, out6, out7
  not not_1 (not_1_out, rd_wr_prime);
  and and_1 (and_1_out, keyReady, writeReady);
  // Probe on cdm_8_1_r3
  // Probe on cdm_8_1_r1
  // Probe on cdm_8_1_r0
  // Probe on cdm_8_1_r2
  Button button_1 (.out(button_1_out));
  and and_2 (clk, ~RAMenable, clock_1_out);  // AND_Gate
  and and_3 (readReady, not_1_out, TTY_Key);
  and and_4 (writeReady, TTY_Key, rd_wr_prime);
  or or_2 (or_2_out, and_5_out, stringEnd);
  and and_5 (and_5_out, stringWrite, not_2_out);
  not not_2 (not_2_out, stringWrite);
  // Probe on cdm_8_1_sp
  // Probe on cdm_8_1_ps
  // Probe on cdm_8_1_pc
  and and_6 (and_6_out, decoder_1_out0, ~rd_wr_prime);  // AND_Gate
  and and_7 (and_7_out, decoder_1_out1, ~rd_wr_prime);  // AND_Gate
  and and_8 (and_8_out, decoder_1_out2, ~rd_wr_prime);  // AND_Gate
  and and_9 (RAMout, decoder_1_out2, rd_wr_prime);
  or or_3 (or_3_out, captureEn, filenameWrite);
  and and_10 (and_10_out, or_3_out, writeReady);
  and and_11 (and_11_out, RAMclr, stringWrite);
  or or_4 (or_4_out, and_11_out, and_1_out);
  or or_5 (or_5_out, writeReady, stringWrite);
  CdM_8 cdm_8_1 (
    .data_code_prime(cdm_8_1_data_code_prime), .R0(cdm_8_1_r0), .R1(cdm_8_1_r1), .mem(cdm_8_1_mem),
    .R2(cdm_8_1_r2), .load_st_prime(rd_wr_prime), .R3(cdm_8_1_r3), .addr(addr), .PC(cdm_8_1_pc),
    .SP(cdm_8_1_sp), .data_out(cdm_8_1_data_out), .data_in(controlled_buffer_2_out), .PS(cdm_8_1_ps),
    .clk(or_1_out), .rset(button_1_out));  // open: page, IAck, IRQ, vector, shadow
  Register #(.trigger("high")) register_1 (.D(IOData), .en(and_6_out), .Q(register_1_q), .clk(and_6_out));  // open: clr
  Register #(.trigger("high")) register_2 (.D(IOData), .en(and_7_out), .Q(register_2_q), .clk(and_7_out));  // open: clr
  Register #(.trigger("high")) register_3 (.D(IOData), .en(and_8_out), .Q(register_3_q), .clk(and_8_out));  // open: clr
  D_Flip_Flop d_ff_1 (.clk(decoder_1_out2), .D(decoder_1_out2), .Q(RAMenable), .reset(RAMclr));  // open: Qn, preset, en
  and and_12 (and_12_out, and_10_out, keyReady);
  Counter counter_1 (.count(or_4_out), .Q(counter_1_q), .clk(or_4_out), .clr(or_2_out));  // open: load, D, carry
  not not_3 (not_3_out, filenameRd);
  not not_4 (not_4_out, captureEn);
  not not_5 (not_5_out, filenameRd);
  not not_6 (not_6_out, stringWrite);
  not not_7 (not_7_out, stringWrite);
  Decoder #(.disabled(0)) decoder_2 (.out0(Inst), .out1(Data), .sel(cdm_8_1_data_code_prime), .en(cdm_8_1_mem));
  assign IOData = not_8_out ? cdm_8_1_data_out : 8'bz;  // Controlled_Buffer controlled_buffer_1
  not not_8 (not_8_out, rd_wr_prime);
  assign controlled_buffer_2_out = rd_wr_prime ? IOData : 8'bz;  // Controlled_Buffer controlled_buffer_2
  or or_6 (or_6_out, readReady, and_12_out);
  or or_7 (or_7_out, stringWrite, captureEn);
  and and_13 (and_13_out[7], writeReady, keyReady, filenameWrite, not_3_out, not_4_out);
  and and_14 (and_14_out, writeReady, not_5_out, stringWrite);
  and and_15 (and_15_out, writeReady, getFile, not_6_out);
  and and_16 (and_16_out[7], filenameRd, writeReady, filenameRd, not_7_out, keyReady);
  or or_8 (or_8_out, RAMenable, and_17_out);
  and and_17 (and_17_out, rd_wr_prime, stringRead);
  assign controlled_buffer_3_out = readReady ? IOData : 8'bz;  // Controlled_Buffer controlled_buffer_3
  assign controlled_buffer_3_out[6:0] = writeReady ? ASCIIrd : 7'bz;  // Controlled_Buffer controlled_buffer_4
  or or_9 (or_9_out, or_6_out, promptClk);
  RAM #(.dataWidth(7), .bus("separate")) ram_1 (
    .addr(counter_1_q), .din(ASCIIrd), .data(writeToRAM), .str(and_1_out), .sel(or_7_out), .clk(and_1_out),
    .ld(or_5_out), .clr(or_10_out));
  or or_10 (or_10_out, stringEnd, bufferClr);
  not not_9 (not_9_out, and_13_out[7]);
  not not_10 (not_10_out, and_15_out);
  not not_11 (not_11_out, and_16_out[7]);
  CheapoRAM cheaporam_1 (
    .Adr({register_1_q, register_2_q}), .En(or_8_out), .Rd_Wr_prime(rd_wr_prime), .D_Out(cheaporam_1_d_out),
    .D_In(register_3_q), .Rdy(RAMclr));
  Pull_Resistor #(.pull(1)) pull_resistor_1 (.node(writeToRAM));
  nor nor_1 (filenameWrStop, and_13_out[7], not_9_out);
  nor nor_2 (filenameRdStart, and_15_out, not_10_out);
  nor nor_3 (filenameRdStop, and_16_out[7], not_11_out);
  ROM rom_1 (.addr(addr), .data(IOData), .sel(Inst));
  // Probe on IOData
  RAM ram_2 (.addr(addr), .data(IOData), .sel(DMEM), .clk(clk), .ld(rd_wr_prime));  // open: clr
  assign IOData = RAMout ? cheaporam_1_d_out : 8'bz;  // Controlled_Buffer controlled_buffer_5
  Multiplexer #(.width(7), .disabled(0), .enable("false")) multiplexer_1 (
    .in0(controlled_buffer_3_out[6:0]), .in1(promptData), .out(multiplexer_1_out), .sel(promptClk));
  not not_12 (not_12_out, or_9_out);
  TTY tty_1 (.data(multiplexer_1_out), .clk(not_13_out), .clr(TTYclr));  // open: we
  not not_13 (not_13_out, not_12_out);
  xor xor_1 (xor_1_out, writeReady, keyClr);
  Keyboard #(.trigger("falling")) keyboard_1 (
    .clk(xor_1_out), .clr(keybrdClr), .avail(keyboard_1_avail), .data(keyboard_1_data));  // open: re
  and EOS (EOS_out, ~writeToRAM[0], ~writeToRAM[1], ~writeToRAM[2], ~writeToRAM[3], ~writeToRAM[4], ~writeToRAM[5], ~writeToRAM[6]);  // AND_Gate
  and and_18 (and_18_out, stringWrite, RAMclr);
  assign IOData = and_13_out[7] ? {and_13_out[7], ASCIIrd} : 8'bz;  // Controlled_Buffer controlled_buffer_6
  assign IOData = and_14_out ? {stringWrite, writeToRAM} : 8'bz;  // Controlled_Buffer controlled_buffer_7
  assign IOData = and_15_out ? readFromRAM : 8'bz;  // Controlled_Buffer controlled_buffer_8
  assign IOData = and_16_out[7] ? {and_16_out[7], ASCIIrd} : 8'bz;  // Controlled_Buffer controlled_buffer_9
  D_Flip_Flop d_ff_2 (.clk(and_18_out), .D(and_18_out), .Q(d_ff_2_q), .reset(stringEnd));  // open: Qn, preset, en
  and and_19 (IOSel, not_14_out, clk, Data);
  assign ASCIIrd = noStringWrite ? keyboard_1_data : 7'bz;  // Controlled_Buffer controlled_buffer_10
  // Probe on ASCIIrd
  assign keyReady = noStringWrite ? keyboard_1_avail : 1'bz;  // Controlled_Buffer controlled_buffer_11
  Pull_Resistor pull_resistor_2 (.node(keyReady));
  and and_20 (stringEnd, EOS_out, and_21_out);
  and and_21 (and_21_out, writeReady, stringWrite, d_ff_2_q);
  not not_14 (not_14_out, nand_1_out);
  and and_22 (DMEM, nand_1_out, Data);
  Pull_Resistor pull_resistor_3 (.node(ASCIIrd));
  nand nand_1 (nand_1_out, addr[3], addr[4], addr[5], addr[6], addr[7]);
  not not_15 (not_15_out, captureEn);
  and and_23 (and_23_out, not_15_out, captureEn);
  not not_16 (not_16_out, filenameWrite);
  and and_24 (and_24_out, not_16_out, filenameWrite);
  not not_17 (not_17_out, filenameRd);
  and and_25 (and_25_out, not_17_out, filenameRd);
  assign bit_extender_1_out = {{5{1'b0}}, priority_encoder_1_out};  // Bit_Extender bit_extender_1
  Priority_Encoder #(.disabled(0)) priority_encoder_1 (
    .in0(stringEnd), .in1(captureEn), .in2(filenameWrite), .in3(filenameRd), .out(priority_encoder_1_out));  // open: in4, in5, in6, in7, en_in, gs, en_out
  Clock clock_2 (.out(clock_2_out));
  // Probe on ASCIIrd
  // Probe on multiplier_1_out
  Multiplier multiplier_1 (.a(bit_extender_1_out), .b(8'h30), .out(multiplier_1_out));  // open: cin, cout
  and Prompt_OK (Prompt_OK_out, ~keyReady, ~stringWrite, ~EOS_2_out);  // AND_Gate
  or or_11 (or_11_out, stringEnd, and_23_out, and_24_out, and_25_out);
  nor nor_4 (nor_4_out, promptClk, not_19_out);
  and and_26 (promptClk, clock_2_out, Prompt_OK_out);
  and s (s_out, ASCIIrd[0], ASCIIrd[1], ~ASCIIrd[2], ~ASCIIrd[3], ASCIIrd[4], ASCIIrd[5], ASCIIrd[6]);  // AND_Gate
  or or_12 (or_12_out, filenameWrite, stringWrite, filenameRd, stringRead);
  and \return  (return_out, ~ASCIIrd[0], ASCIIrd[1], ~ASCIIrd[2], ASCIIrd[3], ~ASCIIrd[4], ~ASCIIrd[5], ~ASCIIrd[6]);  // AND_Gate
  and and_27 (keybrdClr, return_out, captureEn);
  and and_28 (restart, return_out, stringRead);
  or or_13 (or_13_out, stringEnd, bufferClr);
  and r (r_out, ~ASCIIrd[0], ASCIIrd[1], ~ASCIIrd[2], ~ASCIIrd[3], ASCIIrd[4], ASCIIrd[5], ASCIIrd[6]);  // AND_Gate
  and and_29 (and_29_out, r_out, noCapture, noStringWrite, noFilename);
  not not_18 (not_18_out, restart);
  nor nor_5 (nor_5_out, not_18_out, restart);
  Pull_Resistor pull_resistor_4 (.node(pull_resistor_4_node));
  assign pull_resistor_4_node = IOData;  // Buffer buffer_1, 8 bits wide
  S_R_Flip_Flop s_r_ff_1 (.Q(s_r_ff_1_q), .preset(or_11_out), .reset(nor_4_out));  // open: S, clk, R, Qn, en
  not not_19 (not_19_out, promptClk);
  not not_20 (not_20_out, not_21_out);
  not not_21 (not_21_out, clock_3_out);
  D_Flip_Flop #(.trigger("falling")) d_ff_3 (
    .Q(d_ff_3_q), .preset(promptClk), .reset(EOS_2_out));  // open: clk, D, Qn, en
  Clock clock_3 (.out(clock_3_out));
  and and_30 (and_30_out, s_out, ~or_12_out);  // AND_Gate
  Pull_Resistor #(.pull(1)) pull_resistor_5 (.node(pull_resistor_5_node[7]));
  D_Flip_Flop RAM_read_start (
    .clk(and_29_out), .D(and_29_out), .Q(getFile), .reset(filenameRdStart));  // open: Qn, preset, en
  or or_14 (or_14_out, nor_5_out, stringEnd, bufferClr);
  or or_15 (TTYclr, restart, bufferClr, s_r_ff_1_q);
  Counter counter_2 (
    .load(s_r_ff_1_q), .D(multiplier_1_out), .count(d_ff_3_q), .Q(counter_2_q), .clk(not_20_out),
    .clr(or_16_out));  // open: carry
  or or_16 (or_16_out, restart, bufferClr);
  and EOS_2 (EOS_2_out, ~promptData[0], ~promptData[1], ~promptData[2], ~promptData[3], ~promptData[4], ~promptData[5], ~promptData[6]);  // AND_Gate
  D_Flip_Flop String_Capture (
    .clk(and_30_out), .D(and_30_out), .Q(captureEn), .Qn(noCapture), .reset(keybrdClr));  // open: preset, en
  D_Flip_Flop Filename_write_start (
    .clk(keybrdClr), .D(keybrdClr), .Q(filenameWrite), .Qn(noFilename), .reset(filenameWrStop));  // open: preset, en
  D_Flip_Flop RAM_write_start (
    .clk(filenameWrStop), .D(filenameWrStop), .Q(stringWrite), .Qn(noStringWrite), .reset(or_13_out));  // open: preset, en
  D_Flip_Flop Filename_read_start (
    .clk(filenameRdStart), .D(filenameRdStart), .Q(filenameRd), .reset(filenameRdStop));  // open: Qn, preset, en
  D_Flip_Flop String_read_start (
    .clk(filenameRdStop), .D(filenameRdStop), .Q(stringRead), .reset(or_14_out));  // open: Qn, preset, en
  and and_31 (and_31_out, pull_resistor_4_node[0], pull_resistor_4_node[1], pull_resistor_4_node[2], pull_resistor_4_node[3], pull_resistor_4_node[4], pull_resistor_4_node[5], pull_resistor_4_node[6], pull_resistor_4_node[7]);
  not not_22 (not_22_out, captureEn);
  assign readFromRAM = getFile ? {8{pull_resistor_5_node[7]}} : 8'bz;  // Controlled_Buffer controlled_buffer_12
  and and_32 (bufferClr, and_31_out, readReady);
  ROM #(.dataWidth(7)) rom_2 (.addr(counter_2_q), .data(promptData));  // open: sel
  Pull_Resistor #(.pull(1)) pull_resistor_6 (.node(promptData));
  and and_33 (keyClr, not_22_out, captureEn);

  // Other names for the same wires on the sheet: IOAddr[2:0] = addr[2:0]; promptEn = promptClk;
  //   writeToRAM[7] = stringWrite

  // Notes on the sheet:
  //   Filename Write
  //   String Write
  //   Read from RAM
  //   Filename Read
  //   CdM-8 Core w/ Harvard Memory
  //   High Order Addr
  //   Low Order Addr
  //   Data Write
  //   Enable RAM
  //   Slow Access RAM
  //   Read signal
  //   Write Signal
  //   Input Data Logic
  //   I/O
  //   Key Input Buffer
  //   contents of rom_1 (hex, n*v repeats v):
  //   d0 f0 c8 d6 1e d4 c3 d3 f8 ac d3 f9 ad d3 fa ae c7 d7 c3 d3 f8 ac d3 f9 ad d3 fa be c7 d7 d0 fb b1
  //   d3 ff 6 7e e1 2b d6 b9 ee 35 25 e3 33 91 d6 3d ee 35 ee 1e ee 1e d0 fb d1 ff a1 d7 d6 6d d3 ff 7c e0
  //   4a d6 8a d6 4d ee 4c d6 37 d7 c1 c0 c2 3f d0 fb b2 2a e3 63 92 c5 c1 1d 30 d6 6 8f ee 51 ee 6c c5 c4
  //   c6 a2 8c a1 8c a3 d7 d7 c1 c2 d0 0 d2 e0 42 e1 85 b3 f e1 80 c6 c5 3f d7 ee 83 8c 8c 8c ee 71 c6 c5
  //   d0 ff d7 c0 d0 0 d2 e0 42 e1 b8 b2 a e1 a8 0 ed 9d 88 88 ee 9e 8c c1 b1 8c b2 16 c5 c4 d7 ee b6 0 e1
  //   b3 a e1 b3 c4 3a d7 ee b6 8c 8c 8c ee 8d d7 d0 fb b1 25 e2 c3 ee b9 ee e2 91 4 d6 e3 d3 ff 7d e0 e0
  //   d0 fb 3f 7b ed de c2 30 d6 12 d0 fb a2 c6 8d 8f ee cf ee e2 d6 37 d7 d1 0 d2 e0 46 e1 fc b7 73 e1 f7
  //   8d 6 8e b5 ba 3f d7 ee fa 8d 8d 8d ee e5 d1 ff d7
  //   Memory Mapped I/O
  //   User Prompts
  //   buffer_1 drives only 1 and floats otherwise
  //   Command Key Capture
  //   Clear Input Buffer
  //   contents of rom_2 (hex, n*v repeats v):
  //   50 72 65 73 73 20 27 73 27 20 74 6f 20 73 61 76 65 20 61 20 73 74 72 69 6e 67 20 6f 72 20 27 72 27
  //   20 74 6f 20 6c 6f 61 64 20 6f 6e 65 a 0 0 45 6e 74 65 72 20 79 6f 75 72 20 73 74 72 69 6e 67 20 61
  //   6e 64 20 70 72 65 73 73 20 72 65 74 75 72 6e 20 74 6f 20 66 69 6e 69 73 68 a 0 0 0 45 6e 74 65 72 20
  //   61 20 31 20 63 68 61 72 61 63 74 65 72 20 66 69 6c 65 6e 61 6d 65 a 19*0 45 6e 74 65 72 20 66 69 6c
  //   65 6e 61 6d 65 20 6f 66 20 74 68 65 20 73 74 72 69 6e 67 20 28 72 65 74 75 72 6e 20 74 6f 20 65 78
  //   69 74 29 a
endmodule

module Von_Neumann (
  output out_1
);

  wire button_1_out, clk, IOSel, mem, memSel, nand_1_out, not_1_out, not_2_out, rd_wr_prime;
  wire [7:0] addr, cdm_8_1_data_out, cdm_8_1_pc, cdm_8_1_ps, cdm_8_1_r0, cdm_8_1_r1, cdm_8_1_r2, cdm_8_1_r3,
       cdm_8_1_sp, cheaporam_1_d_out, controlled_buffer_1_out;
  wire [15:15] pull_resistor_1_node;

  // Probe on cdm_8_1_r1
  // Probe on cdm_8_1_r2
  // Probe on cdm_8_1_r0
  Button button_1 (.out(button_1_out));
  Clock clock_1 (.out(clk));
  and and_1 (IOSel, not_1_out, clk, mem);
  Pull_Resistor pull_resistor_1 (.node(pull_resistor_1_node[15]));
  // Probe on cdm_8_1_r3
  // Probe on cdm_8_1_sp
  // Probe on cdm_8_1_pc
  not not_1 (not_1_out, nand_1_out);
  and and_2 (memSel, nand_1_out, mem);
  // Probe on cdm_8_1_ps
  nand nand_1 (nand_1_out, addr[0], addr[1], addr[2], addr[3], addr[4], addr[5], addr[6], addr[7]);
  CdM_8 cdm_8_1 (
    .R0(cdm_8_1_r0), .R1(cdm_8_1_r1), .mem(mem), .R2(cdm_8_1_r2), .load_st_prime(rd_wr_prime),
    .R3(cdm_8_1_r3), .addr(addr), .PC(cdm_8_1_pc), .SP(cdm_8_1_sp), .data_out(cdm_8_1_data_out),
    .data_in(controlled_buffer_1_out), .PS(cdm_8_1_ps), .clk(clk), .rset(button_1_out));  // open: data_code_prime, page, IAck, IRQ, vector, shadow
  assign controlled_buffer_1_out = rd_wr_prime ? cheaporam_1_d_out : 8'bz;  // Controlled_Buffer controlled_buffer_1
  CheapoRAM cheaporam_1 (
    .Adr({{8{pull_resistor_1_node[15]}}, addr}), .En(IOSel), .Rd_Wr_prime(rd_wr_prime),
    .D_Out(cheaporam_1_d_out), .D_In(cheaporam_1_d_out), .Rdy(out_1));
  assign cheaporam_1_d_out = not_2_out ? cdm_8_1_data_out : 8'bz;  // Controlled_Buffer controlled_buffer_2
  not not_2 (not_2_out, rd_wr_prime);
  RAM ram_1 (.addr(addr), .data(cheaporam_1_d_out), .sel(memSel), .clk(clk), .ld(rd_wr_prime));  // open: clr
endmodule
