// Logisim project SlowRAM-16x8bit.circ as structural Verilog: 1 circuit, main circuit CheapoRAM
module CheapoRAM (
  input  [15:0] Adr,
  input  [7:0] D_In,
  input  En,
  input  Rd_Wr_prime,
  output [7:0] D_Out,
  output Rdy
);

  wire button_1_out, clock_1_out, not_1_out, not_2_out;
  wire [2:0] counter_1_q;
  wire [7:0] ram_1_data;

  Clock clock_1 (.out(clock_1_out));
  not not_1 (not_1_out, En);
  Button button_1 (.out(button_1_out));
  Counter #(.width(4), .max('hf), .ongoal("stay")) counter_1 (
    .count(En), .Q({Rdy, counter_1_q}), .clk(clock_1_out), .clr(not_1_out));  // open: load, D, carry
  // Probe on ram_1_data
  RAM #(.addrWidth(16)) ram_1 (
    .addr(Adr), .data(ram_1_data), .sel(Rdy), .clk(Rdy), .ld(Rd_Wr_prime), .clr(button_1_out));
  assign D_Out = Rd_Wr_prime ? ram_1_data : 8'bz;  // Controlled_Buffer controlled_buffer_1
  assign ram_1_data = not_2_out ? D_In : 8'bz;  // Controlled_Buffer controlled_buffer_2
  not not_2 (not_2_out, Rd_Wr_prime);
endmodule
